// Logisim project Project.circ as structural Verilog: 2 circuits, main circuit main
module main (
  input  [14:0] in_1,
  input  [14:0] in_2,
  input  [1:0] in_3
);

  wire clock_1_out;
  wire [14:0] adder_1_out, and_1_out, counter_1_q, multiplexer_1_out, or_1_out, register_1_q, rom_1_data,
       xor_1_out;

  Adder #(.width(15)) adder_1 (.a(in_1), .b(in_2), .out(adder_1_out));  // open: cin, cout
  assign and_1_out = in_1 & in_2;  // AND_Gate and_1, 15 bits wide
  assign or_1_out = in_1 | in_2;  // OR_Gate or_1, 15 bits wide
  assign xor_1_out = in_1 ^ in_2;  // XOR_Gate xor_1, 15 bits wide
  Multiplexer #(.select(2), .width(15)) multiplexer_1 (
    .in0(adder_1_out), .in1(and_1_out), .in2(or_1_out), .in3(xor_1_out), .out(multiplexer_1_out), .sel(in_3));  // open: en
  Clock clock_1 (.out(clock_1_out));
  Register #(.width(15)) register_1 (.D(multiplexer_1_out), .Q(register_1_q), .clk(clock_1_out));  // open: en, clr
  Counter #(.width(15), .max('h7fff)) counter_1 (
    .Q(counter_1_q), .clk(clock_1_out));  // open: load, D, count, carry, clr
  // NOR_Gate ZERO has open pins: in0=register_1_q, in1=register_1_q, out=open
  ROM #(.addrWidth(15), .dataWidth(15)) rom_1 (.addr(counter_1_q), .data(rom_1_data));  // open: sel
  Decoder decoder_1 (.IR_IN(rom_1_data));  // open: NOP, ADD, SUB, AND, OR, JMP, OPERAND

  // Notes on the sheet:
  //   contents of rom_1 (hex, n*v repeats v):
  //   800 1000
endmodule

module Decoder (
  input  [14:0] IR_IN,
  output NOP,
  output ADD,
  output SUB,
  output AND,
  output OR,
  output JMP,
  output [10:0] OPERAND
);

  Decoder_part #(.select(4)) decoder_1 (
    .out0(NOP), .out1(ADD), .out2(SUB), .out3(AND), .out4(OR), .out5(JMP), .sel(IR_IN[14:11]));  // open: out6, out7, out8, out9, out10, out11, out12, out13, out14, out15, en

  assign OPERAND = IR_IN[10:0];
endmodule
